# Fritzing sketch Einzelwertanzeige (saved by Fritzing 0.9.3b)
circuit board: 5cm x 8cm
breadboards: 1

parts:
  DI0 = 7-Segment LED Display [package=THT]
  DI1 = 7-Segment LED Display [package=THT]
  Upper_Pinhead = female pin header, 8 pins [form="♀ (female)"]
  Lower_Pinhead = female pin header, 8 pins [form="♀ (female)"]

nets:
  N1: DI0.cathodeE, DI1.cathodeE, Upper_Pinhead.pin6
  N2: DI0.cathodeD, DI1.cathodeD, Lower_Pinhead.pin6
  N3: DI0.commAnode, Upper_Pinhead.pin3
  N4: DI0.cathodeC, DI1.cathodeC, Upper_Pinhead.pin7
  N5: DI0.cathodeDP, DI1.cathodeDP, Upper_Pinhead.pin4
  N6: DI0.cathodeB, DI1.cathodeB, Lower_Pinhead.pin4
  N7: DI0.cathodeA, DI1.cathodeA, Lower_Pinhead.pin3
  N8: DI0.cathodeF, DI1.cathodeF, Upper_Pinhead.pin2
  N9: DI0.cathodeG, DI1.cathodeG, Upper_Pinhead.pin1
  N10: DI1.commAnode, Upper_Pinhead.pin8
