# Fritzing sketch MAX7219 mit 7-Segment-Elementen (saved by Fritzing 0.9.3b)
circuit board: 8.46667cm x 5.64444cm
breadboards: 1

parts:
  U2 = MAX7219 [package=dil24]
  DI1 = 7-Segment LED Display [package=THT]
  DI2 = 7-Segment LED Display [package=THT]

nets:
  N1: U2.DIG0, DI1.commAnode
  N2: U2.DIG1, DI2.commAnode
  N3: U2.SEGA, DI1.cathodeB, DI2.cathodeB
  N4: U2.SEGF, DI1.cathodeG, DI2.cathodeG
  N5: U2.SEGB, DI1.cathodeA, DI2.cathodeA
  N6: U2.SEGG, DI1.cathodeF, DI2.cathodeF
  N7: U2.VCC, DI1.cathodeE, DI2.cathodeE
  N8: U2.SEGC, DI1.cathodeC, DI2.cathodeC
  N9: U2.SEGDP, DI1.cathodeDP, DI2.cathodeDP
  N10: U2.SEGD, DI1.cathodeD, DI2.cathodeD
